# Fritzing sketch pascali-vero (saved by Fritzing 0.9.3b)
circuit board: 6.88566cm x 5.36311cm
stripboards: 2

parts:
  R6 = Resistor [resistance=220 tolerance=±5% package=THT]
  R7 = Resistor [resistance=220 tolerance=±5% package=THT]
  Pressure_Sensor = mystery part, 3 pins [chip_label="Pressure Sensor"]
  Relay = WeMos D1 Mini Relay Shield V2
  Part1 = Arduino Pro Mini v13
  Operation_Indicator = smd LED [color="Green (565nm)" package="0805 [SMD]"]
  Current_Sensor = ACS712 Low Current Sensor Board v12
  Error_Indicator = smd LED [color="Red (633nm)" package="0603 [SMD]"]

nets:
  N1: R6.Pin_0, Operation_Indicator.cathode
  N2: R6.Pin_1, Part1.D9_PWM
  N3: R7.Pin_0, Error_Indicator.anode
  N4: R7.Pin_1, Part1.D8
  GND: Pressure_Sensor.pin1, Relay.G, Part1.GND, Operation_Indicator.anode, Current_Sensor.GND, Error_Indicator.cathode
  5V: Pressure_Sensor.pin2, Relay.5V, Part1.VCC, Current_Sensor.5V
  N5: Pressure_Sensor.pin3, Part1.A0
  N6: Relay.D7, Part1.D4
  N7: Relay.NO, Current_Sensor.IP-
  N8: Part1.A1, Current_Sensor.VO

notes:
  12V supply
  240V Live

// code stored in the sketch: pascali.ino
// pascali intelligent pump controller
// -----------------------------------
// Version 0.1
//
// Functionality
// -------------
// Read pressure sensor and:
// - convert to MPa and display
// - if pressure lower than floor value: start pump
// - if pressure value lower than floor value and pump running
//   for more than 60 seconds : error state
// - if pressure higher that ceiling and pump running: stop pump
//
// To Do
// -----
// - LED display
// - Relay timers
// - Pump current sensor
// - State LEDs (solid green = idle, pulsing green = pump running, red = error)
// - remove delays

// User adjustable parameters
const float low  = 2.0; // MPa
const float high = 3.5; // MPa
const int pressurePin = A0;
const int relayPin = 10;

// Constants and code
const int offset = 20;      // zero pressure adjust
const int fullScale = 1023; // max pressure (span) adjust

// TODO: pin as parameter
float getPressure(const int pin) {
    float reading = analogRead(pin);
    float result = (reading - offset) * 1.2 / (fullScale - offset); // MPa conversion
    return result;
}

// true = on, false = off (default)
// TODO: pin as parameter
//       check logic
bool getRelayState(const int pin) {
    bool state = false; // off
    return state;
}

void setup() {
    Serial.begin(115200);
}

void loop() {

    Serial.print("Pressure: ");
    float pressure = getPressure(pressurePin);
    Serial.print(pressure, 1);
    Serial.println(" MPa");
    Serial.print("pump state: ");
    Serial.println(getRelayState(relayPin) == true ? "on" : "off");

    delay(500);
}
