# Fritzing sketch pascali (saved by Fritzing 0.9.3b)
circuit board: 6.88566cm x 5.36311cm
breadboards: 1

parts:
  R6 = Resistor [resistance=220 tolerance=±5% package=THT]
  LED6 = LED - 5mm [color="Red (633nm)" package="5 mm [THT]"]
  Arduino = Arduino Uno (Rev3)
  LED7 = LED - 5mm [color="Green (555nm)" package="5 mm [THT]"]
  R7 = Resistor [resistance=220 tolerance=±5% package=THT]
  U1 = mystery part, 3 pins [chip_label="Pressure Sensor"]
  WeMos_D1_Mini_Relay_Shield1 = WeMos D1 Mini Relay Shield V2
  Part1 = ACS712 Low Current Sensor Board v12

nets:
  N1: R6.Pin_0, LED6.anode
  N2: R6.Pin_1, Arduino.D4
  GND: LED6.cathode, Arduino.GND, LED7.cathode, U1.pin1, WeMos_D1_Mini_Relay_Shield1.G, Part1.GND
  N3: Arduino.A0, U1.pin3
  N4: Arduino.A1, Part1.VO
  N5: Arduino.D3_PWM, R7.Pin_1
  N6: Arduino.D7, WeMos_D1_Mini_Relay_Shield1.D7
  5V: Arduino.5V, U1.pin2, WeMos_D1_Mini_Relay_Shield1.5V, Part1.5V
  N7: LED7.anode, R7.Pin_0

// code stored in the sketch: pascali.ino
// pascali intelligent pump controller
// -----------------------------------
// Version 0.1
//
// Functionality
// -------------
// Read pressure sensor and:
// - convert to MPa and display
// - if pressure lower than floor value: start pump
// - if pressure value lower than floor value and pump running
//   for more than 60 seconds : error state
// - if pressure higher that ceiling and pump running: stop pump
//
// To Do
// -----
// - LED display
// - Relay timers
// - Pump current sensor
// - State LEDs (solid green = idle, pulsing green = pump running, red = error)
// - remove delays

// User adjustable parameters
const float low  = 2.0; // MPa
const float high = 3.5; // MPa
const int pressurePin = A0;
const int relayPin = 10;

// Constants and code
const int offset = 20;      // zero pressure adjust
const int fullScale = 1023; // max pressure (span) adjust

// TODO: pin as parameter
float getPressure(const int pin) {
    float reading = analogRead(pin);
    float result = (reading - offset) * 1.2 / (fullScale - offset); // MPa conversion
    return result;
}

// true = on, false = off (default)
// TODO: pin as parameter
//       check logic
bool getRelayState(const int pin) {
    bool state = false; // off
    return state;
}

void setup() {
    Serial.begin(115200);
}

void loop() {

    Serial.print("Pressure: ");
    float pressure = getPressure(pressurePin);
    Serial.print(pressure, 1);
    Serial.println(" MPa");
    Serial.print("pump state: ");
    Serial.println(getRelayState(relayPin) == true ? "on" : "off");

    delay(500);
}
